# Fritzing sketch Diagrama electrónico (saved by Fritzing 0.9.3b)
breadboards: 1

parts:
  GY-NEO6MV3 = SUP500F [package=sup500f]
  R3 = Resistor [tolerance=±5% resistance=4.7k package="1206 [SMD]"]
  R4 = Resistor [tolerance=±5% resistance=10k package="1206 [SMD]"]
  YL-83_-_Control_Board1 = YL-83 Rain Sensor - Control Board
  YL-83_-_Detection_Board1 = YL-83 Rain Sensor - Detection Board
  U2 = ESP8266 NodeMCU LoLin module

nets:
  GND: GY-NEO6MV3.RX-I, R4.Pin_1, YL-83_-_Control_Board1.GND, U2.GND
  VCC: GY-NEO6MV3.TX-O, YL-83_-_Control_Board1.VCC, U2.3V3, U2.EN
  N1: GY-NEO6MV3.GND, R3.Pin_1, R4.Pin_0
  N2: GY-NEO6MV3.VCC, U2.D1
  N3: R3.Pin_0, U2.D2
  N4: YL-83_-_Control_Board1.POS, YL-83_-_Detection_Board1.POS
  N5: YL-83_-_Control_Board1.NEG, YL-83_-_Detection_Board1.NEG

notes:
  GND: Black
  VCC: Red
  RX: Yellow
  TX: Green

custom parts:
  YL-83 Rain Sensor - Control Board: The YL-83 is a rain sensor that has more resistance when dry and less resistance when wet. The module runs at 5V.
  YL-83 Rain Sensor - Detection Board: The YL-83 is a rain sensor that has more resistance when dry and less resistance when wet. The module runs at 5V.
  ESP8266 NodeMCU LoLin module: ESP8266 based NodeMCU
